// Logisim project cpu_simple.circ as structural Verilog: 5 circuits, main circuit main
module GRF (
  input  clk,
  input  reset,
  input  [4:0] A1,
  input  [4:0] A2,
  input  WE,
  input  [4:0] A3,
  input  [31:0] WD,
  output [31:0] RD1,
  output [31:0] RD2
);

  wire _0i, _1i, _2i, _3i, _4i, _5i, _6i, _7i, _8i, _9i, _10i, _11i, _12i, _13i, _14i, _15i, _16i, _17i,
       _18i, _19i, _20i, _21i, _22i, _23i, _24i, _25i, _26i, _27i, _28i, _29i, _30i, _31i;
  wire [31:0] _0o, _1o, _2o, _3o, _4o, _5o, _6o, _7o, _8o, _9o, _10o, _11o, _12o, _13o, _14o, _15o, _16o,
       _17o, _18o, _19o, _20o, _21o, _22o, _23o, _24o, _25o, _26o, _27o, _28o, _29o, _30o, _31o;

  Demultiplexer #(.select(5), .disabled(0)) demultiplexer_1 (
    .out0(_0i), .out1(_1i), .out2(_2i), .out3(_3i), .out4(_4i), .out5(_5i), .out6(_6i), .out7(_7i),
    .out8(_8i), .out9(_9i), .out10(_10i), .out11(_11i), .out12(_12i), .out13(_13i), .out14(_14i),
    .out15(_15i), .out16(_16i), .out17(_17i), .out18(_18i), .out19(_19i), .out20(_20i), .out21(_21i),
    .out22(_22i), .out23(_23i), .out24(_24i), .out25(_25i), .out26(_26i), .out27(_27i), .out28(_28i),
    .out29(_29i), .out30(_30i), .out31(_31i), .in(1'b1), .sel(A3), .en(WE));
  Register #(.width(32)) _0 (.D({32{1'b0}}), .en(_0i), .Q(_0o), .clk(clk), .clr(reset));
  Register #(.width(32)) _1 (.D(WD), .en(_1i), .Q(_1o), .clk(clk), .clr(reset));
  Register #(.width(32)) _1_2 (.D(WD), .en(_2i), .Q(_2o), .clk(clk), .clr(reset));
  Register #(.width(32)) _1_3 (.D(WD), .en(_3i), .Q(_3o), .clk(clk), .clr(reset));
  Register #(.width(32)) _1_4 (.D(WD), .en(_4i), .Q(_4o), .clk(clk), .clr(reset));
  Register #(.width(32)) _1_5 (.D(WD), .en(_5i), .Q(_5o), .clk(clk), .clr(reset));
  Register #(.width(32)) _1_6 (.D(WD), .en(_6i), .Q(_6o), .clk(clk), .clr(reset));
  Register #(.width(32)) _1_7 (.D(WD), .en(_7i), .Q(_7o), .clk(clk), .clr(reset));
  Register #(.width(32)) _1_8 (.D(WD), .en(_8i), .Q(_8o), .clk(clk), .clr(reset));
  Register #(.width(32)) _1_9 (.D(WD), .en(_9i), .Q(_9o), .clk(clk), .clr(reset));
  Register #(.width(32)) _1_10 (.D(WD), .en(_10i), .Q(_10o), .clk(clk), .clr(reset));
  Register #(.width(32)) _1_11 (.D(WD), .en(_11i), .Q(_11o), .clk(clk), .clr(reset));
  Register #(.width(32)) _1_12 (.D(WD), .en(_12i), .Q(_12o), .clk(clk), .clr(reset));
  Register #(.width(32)) _1_13 (.D(WD), .en(_13i), .Q(_13o), .clk(clk), .clr(reset));
  Register #(.width(32)) _1_14 (.D(WD), .en(_14i), .Q(_14o), .clk(clk), .clr(reset));
  Register #(.width(32)) _1_15 (.D(WD), .en(_15i), .Q(_15o), .clk(clk), .clr(reset));
  Register #(.width(32)) _1_16 (.D(WD), .en(_16i), .Q(_16o), .clk(clk), .clr(reset));
  Register #(.width(32)) _1_17 (.D(WD), .en(_17i), .Q(_17o), .clk(clk), .clr(reset));
  Register #(.width(32)) _1_18 (.D(WD), .en(_18i), .Q(_18o), .clk(clk), .clr(reset));
  Register #(.width(32)) _1_19 (.D(WD), .en(_19i), .Q(_19o), .clk(clk), .clr(reset));
  Register #(.width(32)) _1_20 (.D(WD), .en(_20i), .Q(_20o), .clk(clk), .clr(reset));
  Register #(.width(32)) _1_21 (.D(WD), .en(_21i), .Q(_21o), .clk(clk), .clr(reset));
  Register #(.width(32)) _1_22 (.D(WD), .en(_22i), .Q(_22o), .clk(clk), .clr(reset));
  Register #(.width(32)) _1_23 (.D(WD), .en(_23i), .Q(_23o), .clk(clk), .clr(reset));
  Register #(.width(32)) _1_24 (.D(WD), .en(_24i), .Q(_24o), .clk(clk), .clr(reset));
  Register #(.width(32)) _1_25 (.D(WD), .en(_25i), .Q(_25o), .clk(clk), .clr(reset));
  Register #(.width(32)) _1_26 (.D(WD), .en(_26i), .Q(_26o), .clk(clk), .clr(reset));
  Register #(.width(32)) _1_27 (.D(WD), .en(_27i), .Q(_27o), .clk(clk), .clr(reset));
  Register #(.width(32)) _1_28 (.D(WD), .en(_28i), .Q(_28o), .clk(clk), .clr(reset));
  Register #(.width(32)) _1_29 (.D(WD), .en(_29i), .Q(_29o), .clk(clk), .clr(reset));
  Register #(.width(32)) _1_30 (.D(WD), .en(_30i), .Q(_30o), .clk(clk), .clr(reset));
  Register #(.width(32)) _1_31 (.D(WD), .en(_31i), .Q(_31o), .clk(clk), .clr(reset));
  Multiplexer #(.select(5), .width(32)) multiplexer_1 (
    .in0(_0o), .in1(_1o), .in2(_2o), .in3(_3o), .in4(_4o), .in5(_5o), .in6(_6o), .in7(_7o), .in8(_8o),
    .in9(_9o), .in10(_10o), .in11(_11o), .in12(_12o), .in13(_13o), .in14(_14o), .in15(_15o), .in16(_16o),
    .in17(_17o), .in18(_18o), .in19(_19o), .in20(_20o), .in21(_21o), .in22(_22o), .in23(_23o), .in24(_24o),
    .in25(_25o), .in26(_26o), .in27(_27o), .in28(_28o), .in29(_29o), .in30(_30o), .in31(_31o), .out(RD1),
    .sel(A1));  // open: en
  Multiplexer #(.select(5), .width(32)) multiplexer_2 (
    .in0(_0o), .in1(_1o), .in2(_2o), .in3(_3o), .in4(_4o), .in5(_5o), .in6(_6o), .in7(_7o), .in8(_8o),
    .in9(_9o), .in10(_10o), .in11(_11o), .in12(_12o), .in13(_13o), .in14(_14o), .in15(_15o), .in16(_16o),
    .in17(_17o), .in18(_18o), .in19(_19o), .in20(_20o), .in21(_21o), .in22(_22o), .in23(_23o), .in24(_24o),
    .in25(_25o), .in26(_26o), .in27(_27o), .in28(_28o), .in29(_29o), .in30(_30o), .in31(_31o), .out(RD2),
    .sel(A2));  // open: en

  // Other names for the same wires on the sheet: in[31:0] = WD
endmodule

module ALU (
  input  [31:0] Data1,
  input  [31:0] Data2,
  input  [1:0] Option,
  output [31:0] Data_out,
  output Zero
);

  wire comparator_1_eq;
  wire [31:0] adder_1_out, or_1_out, subtractor_1_out;

  Adder #(.width(32)) adder_1 (.a(Data1), .b(Data2), .out(adder_1_out));  // open: cin, cout
  Subtractor #(.width(32)) subtractor_1 (.a(Data1), .b(Data2), .out(subtractor_1_out));  // open: bin, bout
  assign or_1_out = Data1 | Data2;  // OR_Gate or_1, 32 bits wide
  Multiplexer #(.select(2), .width(32)) multiplexer_1 (
    .in0(adder_1_out), .in1(subtractor_1_out), .in2(or_1_out), .in3(subtractor_1_out), .out(Data_out),
    .sel(Option));  // open: en
  Comparator #(.width(32)) comparator_1 (.a(Data_out), .b({32{1'b0}}), .eq(comparator_1_eq));  // open: gt, lt
  Multiplexer #(.select(2)) multiplexer_2 (
    .in0(1'b0), .in1(1'b0), .in2(1'b0), .in3(comparator_1_eq), .out(Zero), .sel(Option));  // open: en
endmodule

module main (
  input  Reset,
  output [31:0] Instr,
  output RegWrite,
  output [4:0] RegAddr,
  output [31:0] RegData,
  output MemWrite,
  output [4:0] MemAddr,
  output [31:0] MemData
);

  wire alu_1_zero, Clk, controler_1_alu_in, controler_1_extend_sel1, controler_1_extend_sel2,
       controler_1_grf_add, controler_1_mem_grf, controler_1_mem_out;
  wire [1:0] controler_1_option;
  wire [29:0] bit_extender_3_out;
  wire [31:0] adder_1_out, alu_1_data_out, bit_extender_1_out, bit_extender_2_out, grf_1_rd1, ifu_1_pc_out,
       multiplexer_1_out, multiplexer_2_out, multiplexer_4_out, multiplexer_5_out, ram_1_data;

  Clock u_Clk (.out(Clk));
  // Probe on ifu_1_pc_out
  IFU ifu_1 (.PC_next(multiplexer_5_out), .Clk(Clk), .Reset(Reset), .PC_out(ifu_1_pc_out), .IM_out(Instr));
  assign bit_extender_1_out = {{16{1'b0}}, Instr[15:0]};  // Bit_Extender bit_extender_1
  Multiplexer #(.width(32)) multiplexer_1 (
    .in0({Instr[15:0], {16{1'b0}}}), .in1(bit_extender_1_out), .out(multiplexer_1_out),
    .sel(controler_1_extend_sel2));  // open: en
  assign bit_extender_2_out = {{16{Instr[15]}}, Instr[15:0]};  // Bit_Extender bit_extender_2
  Controler controler_1 (
    .Op(Instr[31:26]), .Func(Instr[5:0]), .Option(controler_1_option), .GRF_Add(controler_1_grf_add),
    .Mem_GRF(controler_1_mem_grf), .ALU_in(controler_1_alu_in), .Mem_out(controler_1_mem_out),
    .Mem_in(MemWrite), .GRF_WE(RegWrite), .Extend_sel1(controler_1_extend_sel1),
    .Extend_sel2(controler_1_extend_sel2));
  Multiplexer #(.width(32)) multiplexer_2 (
    .in0(bit_extender_2_out), .in1(multiplexer_1_out), .out(multiplexer_2_out), .sel(controler_1_extend_sel1));  // open: en
  Multiplexer #(.width(5)) multiplexer_3 (
    .in0(Instr[20:16]), .in1(Instr[15:11]), .out(RegAddr), .sel(controler_1_grf_add));  // open: en
  // Probe on multiplexer_5_out
  GRF grf_1 (
    .A1(Instr[25:21]), .A3(RegAddr), .A2(Instr[20:16]), .WD(RegData), .RD1(grf_1_rd1), .RD2(MemData),
    .clk(Clk), .reset(Reset), .WE(RegWrite));
  assign bit_extender_3_out = {{14{Instr[15]}}, Instr[15:0]};  // Bit_Extender bit_extender_3
  Multiplexer #(.width(32)) multiplexer_4 (
    .in0(MemData), .in1(multiplexer_2_out), .out(multiplexer_4_out), .sel(controler_1_alu_in));  // open: en
  // Probe on adder_1_out
  Adder #(.width(32)) adder_1 (
    .a(ifu_1_pc_out), .b({bit_extender_3_out, 2'b00}), .out(adder_1_out));  // open: cin, cout
  ALU alu_1 (
    .Data1(grf_1_rd1), .Data2(multiplexer_4_out), .Option(controler_1_option),
    .Data_out({alu_1_data_out[31:7], MemAddr, alu_1_data_out[1:0]}), .Zero(alu_1_zero));
  Multiplexer #(.width(32)) multiplexer_5 (
    .in0(ifu_1_pc_out), .in1(adder_1_out), .out(multiplexer_5_out), .sel(alu_1_zero));  // open: en
  RAM #(.addrWidth(5), .dataWidth(32), .bus("separate")) ram_1 (
    .addr(MemAddr), .din(MemData), .data(ram_1_data), .str(MemWrite), .clk(Clk), .ld(controler_1_mem_out),
    .clr(Reset));  // open: sel
  Multiplexer #(.width(32)) multiplexer_6 (
    .in0(ram_1_data), .in1({alu_1_data_out[31:7], MemAddr, alu_1_data_out[1:0]}), .out(RegData),
    .sel(controler_1_mem_grf));  // open: en

  // Notes on the sheet:
  //   Option
  //   Function
  //   Rs
  //   Rt
  //   Rd
  //   16bits
  //   Extend-sel2
  //   Extend-sel1
  //   GRF-Add
  //   ALU-in
  //   Mem-GRF
endmodule

module IFU (
  input  [31:0] PC_next,
  input  Clk,
  input  Reset,
  output [31:0] PC_out,
  output [31:0] IM_out
);

  wire [31:0] PC_q;

  Register #(.width(32)) PC (.D(PC_next), .Q(PC_q), .clk(Clk), .clr(Reset));  // open: en
  Adder #(.width(32)) adder_1 (.a(32'h4), .b(PC_q), .out(PC_out));  // open: cin, cout
  ROM #(.addrWidth(5), .dataWidth(32)) rom_1 (.addr(PC_q[6:2]), .data(IM_out));  // open: sel

  // Notes on the sheet:
  //   contents of rom_1 (hex, n*v repeats v):
  //   ac010004 341c0000 341d0000 340080f8 36ee0367 3593769c 34dda539 ac010004 3465c5dc 34be0ff1 3472af1d
  //   35fe72a7 3437ff23 37b9649e 3690bf9b 37fe4e0c 3711f49d 3c113bfe 3c057433 3c03c451 3c04c431 3c1c24d9
  //   3c1bf0da 3c0ccc68 3c0a118d 3c1021ea 3c0004d3 3c16115b 3c184f06 3c1215de 1000ffff
endmodule

module Controler (
  input  [5:0] Op,
  input  [5:0] Func,
  output [1:0] Option,
  output Extend_sel2,
  output GRF_Add,
  output Mem_GRF,
  output ALU_in,
  output Mem_out,
  output Mem_in,
  output GRF_WE,
  output Extend_sel1
);

  wire Addu_out, and_1_out, Beq_out, Lui_out, Nop_out, Subu_out;

  and and_1 (and_1_out, ~Op[5], ~Op[4], ~Op[3], ~Op[2], ~Op[1], ~Op[0]);  // AND_Gate
  and Addu (Addu_out, Func[5], ~Func[4], ~Func[3], ~Func[2], ~Func[1], Func[0], and_1_out);  // AND_Gate
  or or_1 (GRF_Add, Addu_out, Subu_out);
  and Subu (Subu_out, Func[5], ~Func[4], ~Func[3], ~Func[2], Func[1], Func[0], and_1_out);  // AND_Gate
  and Nop (Nop_out, ~Func[5], ~Func[4], ~Func[3], ~Func[2], ~Func[1], ~Func[0], and_1_out);  // AND_Gate
  or or_2 (Mem_GRF, Addu_out, Subu_out, Extend_sel2, Lui_out);
  and Ori (Extend_sel2, ~Op[5], ~Op[4], Op[3], Op[2], ~Op[1], Op[0]);  // AND_Gate
  or or_3 (ALU_in, Extend_sel2, Mem_out, Lui_out, Mem_in);
  and Lw (Mem_out, Op[5], ~Op[4], ~Op[3], ~Op[2], Op[1], Op[0]);  // AND_Gate
  and Sw (Mem_in, Op[5], ~Op[4], Op[3], ~Op[2], Op[1], Op[0]);  // AND_Gate
  and Beq (Beq_out, ~Op[5], ~Op[4], ~Op[3], Op[2], ~Op[1], ~Op[0]);  // AND_Gate
  or or_4 (GRF_WE, Mem_out, Extend_sel2, Addu_out, Subu_out, Lui_out);
  and Lui (Lui_out, ~Op[5], ~Op[4], Op[3], Op[2], Op[1], Op[0]);  // AND_Gate
  or or_5 (Option[1], Beq_out, Extend_sel2);
  or or_6 (Option[0], Beq_out, Subu_out);
  or or_7 (Extend_sel1, Lui_out, Extend_sel2);
endmodule
